# Fritzing sketch SPEAKER_SD (saved by Fritzing 0.9.3b)
breadboards: 1

parts:
  Componente1 = Adafruit MAX98357A I2S 3W Class D Amplifier [part_number="Adafruit #3006"]
  U2 = ESP32-38PinWide [part_number=ESP32-38PinWide]
  Componente2 = Adafruit MicroSD card breakout board [part_number="Adafruit #254"]

nets:
  N1: Componente1.VIN, U2.3.3
  GND: Componente1.GND, U2.GND, Componente2.GND
  N2: Componente1.DIN, U2.GPIO25
  N3: Componente1.BCLK, U2.GPIO27
  N4: Componente1.LRCLK, U2.GPIO26
  VIN: U2.VIN, Componente2.VCC
  N5: U2.GPIO5, Componente2.CS
  N6: U2.GPIO18, Componente2.CLK
  N7: U2.GPIO19, Componente2.DO
  N8: U2.GPIO23, Componente2.DI

notes:
  LRC: G26
  BCLK: G27
  DIN/DOUT: G25
  VCC: 3.3V (3.3~5V)
  By connecting a pullup or pull down resistor, or wiring directly, the Gain pin can be set up to give 3dB, 6dB, 9dB, 12dB or 15dB.
  CS: G5
  MOSI: G23
  MISO: G19
  SCLK: G18
  VCC: 5V
  2022 © Dott. Daniel Rossi

custom parts:
  Adafruit MAX98357A I2S 3W Class D Amplifier: Listen to this good news - we now have an all in one digital audio amp breakout board that works incredibly well with the Raspberry Pi! If you're looking for an easy and low cost way to get you digital sound files bumpin' then the MAX08357 I2S Amp Breakout is for you. It takes standard I2S digital audio input and, not only decodes it into analog, but also amplifies it directly into a speaker.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
  ESP32-38PinWide: Generic 38-Pin ESP32 with wide format (only access to one side of pins on a breadboard) based on Stephen Lilley's HiLetgo ESP-WROOM-32 ESP32 ESP-32S Development Board.
  Adafruit MicroSD card breakout board: Not just a simple breakout board, this microSD adapter goes the extra mile - designed for ease of use. Onboard 5v->3v regulator provides 150mA for power-hungry cards 3v level shifting means you can use this with ease on either 3v or 5v systems Uses a proper level shifting chip, not resistors: less problems, and faster read/write access Use 3 or 4 digital pins to read and write 2Gb+ of storage!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
