# Fritzing sketch ESP32 Web Server (saved by Fritzing 0.9.3b)
breadboards: 1

parts:
  U1 = esp32_V2
  T1 = LM35 Temperature Sensor [package="TO92 [THT]"]
  LED1 = LED - 3mm [color="Red (633nm)" package="3 mm [THT]"]
  R1 = Resistor [tolerance=±5% resistance=330 package="0805 [SMD]"]
  LED2 = LED - 3mm [color="Red (633nm)" package="3 mm [THT]"]
  R2 = Resistor [tolerance=±5% resistance=330 package="0805 [SMD]"]

nets:
  N1: U1.connector18, T1.+Vs
  N2: U1.connector19, T1.GND, LED1.cathode, LED2.cathode
  N3: U1.connector42, T1.Vout
  N4: LED1.anode, R1.Pin_0
  N5: LED2.anode, R2.Pin_0

notes:
  ESP32 Web Server
  - breadboard voltage: 5V
  officialprojecto.wordpress.com
